# Fritzing sketch Untitled Sketch (saved by Fritzing 0.9.2b)
perfboards: 1

parts:
  ESP8266-1 = ESP8266-12 [part_number=ESP8266-12]
  U1 = V_REG_LD1117VXX [package=78xxl]
  X1 = USB Connectors [package=usb-microb]
  IC1 = ATMega8 [package=dil28-3-zif_socket]
  Part1 = Logic Level Converter
  Q2 = NPN-Transistor [package="TO92 [THT]"]
  D1 = LTE-302 [package=lte-302]
  R1 = Resistor [tolerance=±5% resistance=470 package="0805 [SMD]"]
  C2 = Capacitor Polarized [package=panasonic_g]
  C1 = Capacitor Polarized [package=panasonic_g]

nets:
  N1: ESP8266-1.CH_PD, ESP8266-1.VCC, U1.OUT, Part1.LV
  N2: ESP8266-1.TXD, Part1.TX2_LV
  N3: ESP8266-1.RXD, Part1.TX_LV
  GND: U1.GND, X1.GND, IC1.GND, Part1.GND, Q2.E, C2.-, C1.-
  N4: U1.IN, X1.VBUS, IC1.VCC, Part1.HV, R1.Pin_0, C2.+, C1.+
  N5: IC1.PD0(RXD), Part1.TX2_HV
  N6: IC1.PD1(TXD), Part1.TX_HV
  N7: IC1.PB0(ICP), Q2.B
  N8: Q2.C, D1.C
  N9: D1.A, R1.Pin_1

custom parts:
  ATMega8: MICROCONTROLLER 8 Kbytes FLASH 1 kbytes SRAM 512 bytes EEPROM USART 4-channel 10 bit ADC 2-channel 8 bit ADC
