# Fritzing sketch perfboard (saved by Fritzing 0.9.2b)
perfboards: 1

parts:
  IC1 = ATMega8 [package=dil28-3-zif_socket]
  ESP8266-1 = ESP8266-12 [part_number=ESP8266-12]
  Q2 = MOSFET-NCHANNEL [package=to-92]
  X1 = USB Connectors [package=usb-microb]
  Q3 = TRANSISTOR_NPN [package=to-92-ammo]
  IC2 = V_REG_LD1117VXX [package=78xxl]
  J1 = female pin header, 4 pins [form="♀ (female)"]
  LED1 = LED - 5mm [color="Red (633nm)" package="5 mm [THT]"]
  LED2 = LED - 5mm [color="Infrared (850nm)" package="5 mm [THT]"]

nets:
  N1: IC1.PD1(TXD), Q2.D
  N2: IC1.VCC, X1.VBUS, IC2.IN
  GND: IC1.GND, ESP8266-1.GPIO15, ESP8266-1.GND, X1.GND, IC2.GND
  N3: IC1.PB1(OC1A), Q3.B
  N4: ESP8266-1.CH_PD, ESP8266-1.VCC, ESP8266-1.GPIO2, IC2.OUT, J1.pin2
  N5: ESP8266-1.RXD, Q2.S, J1.pin3
  N6: Q3.E, LED2.cathode
  N7: LED1.cathode, LED2.anode

custom parts:
  ATMega8: MICROCONTROLLER 8 Kbytes FLASH 1 kbytes SRAM 512 bytes EEPROM USART 4-channel 10 bit ADC 2-channel 8 bit ADC
